# Fritzing sketch Analog(OUTPUT) (saved by Fritzing 0.9.3b)
breadboards: 1

parts:
  부품1 = Arduino Uno (Rev3)
  R3 = Rotary Potentiometer (Small) [maximum_resistance=100kΩ package=THT]
  LED1 = LED - 5mm [color="Red (633nm)" package="5 mm [THT]"]
  R4 = Resistor [tolerance=±5% resistance=220 package=THT]

nets:
  N1: 부품1.A0, R3.wiper
  N2: 부품1.D10_PWM/SS, LED1.anode
  N3: 부품1.GND, R3.leg2, R4.Pin_0
  N4: 부품1.5V, R3.leg1
  N5: LED1.cathode, R4.Pin_1
