# Fritzing sketch LED깜박이기 (saved by Fritzing 0.9.3b)
breadboards: 1

parts:
  부품1 = Arduino Uno (Rev3)
  R1 = Resistor [tolerance=±5% resistance=220 package=THT]
  LED6 = LED - 5mm [color="Red (633nm)" package="5 mm [THT]"]
  LED7 = LED - 5mm [color="Red (633nm)" package="5 mm [THT]"]
  LED8 = LED - 5mm [color="Red (633nm)" package="5 mm [THT]"]
  LED9 = LED - 5mm [color="Red (633nm)" package="5 mm [THT]"]
  LED10 = LED - 5mm [color="Red (633nm)" package="5 mm [THT]"]
  LED11 = LED - 5mm [color="Red (633nm)" package="5 mm [THT]"]

nets:
  N1: 부품1.GND, R1.Pin_0
  N2: 부품1.D2, LED6.anode
  N3: 부품1.D3_PWM, LED7.anode
  N4: 부품1.D4, LED8.anode
  N5: 부품1.D5_PWM, LED9.anode
  N6: 부품1.D6_PWM, LED10.anode
  N7: 부품1.D7, LED11.anode
  N8: R1.Pin_1, LED6.cathode, LED7.cathode, LED8.cathode, LED9.cathode, LED10.cathode, LED11.cathode
