# Fritzing sketch LED깜박이기(Senser) (saved by Fritzing 0.9.3b)
breadboards: 1

parts:
  부품1 = Arduino Uno (Rev3)
  LED11 = LED - 5mm [color="Red (633nm)" package="5 mm [THT]"]
  R1 = Resistor [tolerance=±5% resistance=220 package=THT]
  부품2 = HC-SR501 Body Sensor Module

nets:
  N1: 부품1.D10_PWM/SS, LED11.anode
  GND: 부품1.GND, R1.Pin_0, 부품2.GND
  N2: 부품1.D2, 부품2.OUT
  5V: 부품1.5V, 부품2.VCC
  N3: LED11.cathode, R1.Pin_1

custom parts:
  HC-SR501 Body Sensor Module: Pyroelectric Infrared PIR Motion Sensor Detector Module
